# Fritzing sketch Photoresistor Interrupter (saved by Fritzing 0.8.7b)
breadboards: 1

parts:
  R1 = Resistor [tolerance=±5% resistance=680 package=THT]
  LED1 = LED - 5mm [color="Red (633nm)" package="5 mm [THT]"]
  Part1 = Arduino Uno (Rev3)
  R2 = Photocell (LDR) [package=THT]
  R3 = Resistor [tolerance=±5% resistance=68k package=THT]

nets:
  N1: R1.Pin_0, Part1.5V, R3.Pin_0
  N2: R1.Pin_1, LED1.cathode
  N3: LED1.anode, Part1.GND, R2.pin_1
  N4: Part1.A0, R2.pin_0, R3.Pin_1
